# Fritzing sketch DC_Motor_Speed_Control (saved by Fritzing 0.9.4)
stripboards: 1

parts:
  R1 = Resistor [tolerance=±5% resistance=280 package=THT]
  Q1 = NPN-Transistor [package="TO92 [THT]"]
  D1 = Rectifier Diode [part_number=1N4001 package="300 mil [THT]"]
  M1 = DC Motor
  Part1 = Arduino Uno (Rev3)

nets:
  N1: R1.Pin_0, Q1.B
  N2: R1.Pin_1, Part1.D9_PWM
  N3: Q1.E, Part1.3V3
  N4: Q1.C, D1.cathode, M1.pin_2
  N5: D1.anode, M1.pin_1, Part1.GND

notes:
  Use breakaway pin for resistor
  Pin9=PWM
  DC Volt
  DC GND
  PWR GND
  PWR Volt
